// Logisim project EP01.circ as structural Verilog: 7 circuits, main circuit fullbitAdder
module fullbitAdder (
  input  cin,
  input  a0,
  input  b0,
  output s0,
  output cout
);

  wire and_1_out, and_2_out, xor_1_out;

  xor xor_1 (xor_1_out, a0, b0);
  and and_1 (and_1_out, a0, b0);
  xor xor_2 (s0, cin, xor_1_out);
  and and_2 (and_2_out, cin, xor_1_out);
  or or_1 (cout, and_2_out, and_1_out);
endmodule

module Full_Adder (
  input  A0,
  input  Ci,
  input  A1,
  input  A2,
  input  A3,
  input  B0,
  input  B1,
  input  B2,
  input  B3,
  output S0,
  output S1,
  output S2,
  output S3,
  output Overflow
);

  wire decoder_1_out_5, decoder_1_out_6, decoder_1_out_7, decoder_1_out_8, decoder_1_out_9, decoder_1_out_10,
       decoder_1_out_11, decoder_1_out_12, decoder_2_out_5, decoder_2_out_6, decoder_2_out_7,
       decoder_2_out_8, decoder_2_out_9, decoder_2_out_10, decoder_2_out_11, decoder_2_out_12,
       decoder_3_out_5, decoder_3_out_6, decoder_3_out_7, decoder_3_out_8, decoder_3_out_9, decoder_3_out_10,
       decoder_3_out_11;

  Decoder decoder_1 (
    .e0(A0), .e1(A1), .e2(A2), .e3(A3), .out_5(decoder_1_out_5), .out_6(decoder_1_out_6),
    .out_7(decoder_1_out_7), .out_8(decoder_1_out_8), .out_9(decoder_1_out_9), .out_10(decoder_1_out_10),
    .out_11(decoder_1_out_11), .out_12(decoder_1_out_12));
  Decoder decoder_2 (
    .e0(B0), .e1(B1), .e2(B2), .e3(B3), .out_5(decoder_2_out_5), .out_6(decoder_2_out_6),
    .out_7(decoder_2_out_7), .out_8(decoder_2_out_8), .out_9(decoder_2_out_9), .out_10(decoder_2_out_10),
    .out_11(decoder_2_out_11), .out_12(decoder_2_out_12));
  _4bitAdder u_4bitadder_1 (
    .cin(Ci), .in_2(A0), .in_3(A1), .in_4(A2), .in_5(A3), .in_6(B0), .in_7(B1), .in_8(B2), .in_9(B3),
    .out_10(S0), .out_11(S1), .out_12(S2), .out_13(S3), .over(Overflow));
  _7_Segment_Display u_7_segment_display_1 (
    .g(decoder_1_out_5), .f(decoder_1_out_6), .a(decoder_1_out_7), .b(decoder_1_out_8), .e(decoder_1_out_9),
    .d(decoder_1_out_10), .c(decoder_1_out_11), .dp(decoder_1_out_12));
  _7_Segment_Display u_7_segment_display_2 (
    .g(decoder_2_out_5), .f(decoder_2_out_6), .a(decoder_2_out_7), .b(decoder_2_out_8), .e(decoder_2_out_9),
    .d(decoder_2_out_10), .c(decoder_2_out_11), .dp(decoder_2_out_12));
  Decoder decoder_3 (
    .e0(S0), .e1(S1), .e2(S2), .e3(S3), .out_5(decoder_3_out_5), .out_6(decoder_3_out_6),
    .out_7(decoder_3_out_7), .out_8(decoder_3_out_8), .out_9(decoder_3_out_9), .out_10(decoder_3_out_10),
    .out_11(decoder_3_out_11));  // open: out_12
  _7_Segment_Display u_7_segment_display_3 (
    .g(decoder_3_out_5), .f(decoder_3_out_6), .a(decoder_3_out_7), .b(decoder_3_out_8), .e(decoder_3_out_9),
    .d(decoder_3_out_10), .c(decoder_3_out_11), .dp(Overflow));
endmodule

module _4bitAdder (
  input  cin,
  input  in_2,
  input  in_3,
  input  in_4,
  input  in_5,
  input  in_6,
  input  in_7,
  input  in_8,
  input  in_9,
  output out_10,
  output out_11,
  output out_12,
  output out_13,
  output over
);

  wire fullbitadder_1_cout, fullbitadder_2_cout, fullbitadder_3_cout;

  fullbitAdder fullbitadder_1 (.cin(cin), .a0(in_2), .b0(in_6), .s0(out_10), .cout(fullbitadder_1_cout));
  fullbitAdder fullbitadder_2 (
    .cin(fullbitadder_1_cout), .a0(in_3), .b0(in_7), .s0(out_11), .cout(fullbitadder_2_cout));
  fullbitAdder fullbitadder_3 (
    .cin(fullbitadder_2_cout), .a0(in_4), .b0(in_8), .s0(out_12), .cout(fullbitadder_3_cout));
  fullbitAdder fullbitadder_4 (.cin(fullbitadder_3_cout), .a0(in_5), .b0(in_9), .s0(out_13), .cout(over));
endmodule

module _4bitAdder_neg (
  input  cin,
  input  in_2,
  input  in_3,
  input  in_4,
  input  in_5,
  input  in_6,
  input  in_7,
  input  in_8,
  input  in_9,
  output out_10,
  output out_11,
  output out_12,
  output out_13,
  output over
);

  wire fullbitadder_1_cout, fullbitadder_2_cout, fullbitadder_3_cout, fullbitadder_4_cout;

  fullbitAdder fullbitadder_1 (.cin(cin), .a0(in_2), .b0(in_6), .s0(out_10), .cout(fullbitadder_1_cout));
  fullbitAdder fullbitadder_2 (
    .cin(fullbitadder_1_cout), .a0(in_3), .b0(in_7), .s0(out_11), .cout(fullbitadder_2_cout));
  fullbitAdder fullbitadder_3 (
    .cin(fullbitadder_2_cout), .a0(in_4), .b0(in_8), .s0(out_12), .cout(fullbitadder_3_cout));
  fullbitAdder fullbitadder_4 (
    .cin(fullbitadder_3_cout), .a0(in_5), .b0(in_9), .s0(out_13), .cout(fullbitadder_4_cout));
  xor xor_1 (over, fullbitadder_3_cout, fullbitadder_4_cout);
endmodule

module Decoder (
  input  e0,
  input  e1,
  input  e2,
  input  e3,
  output out_5,
  output out_6,
  output out_7,
  output out_8,
  output out_9,
  output out_10,
  output out_11,
  output out_12
);

  Multiplexer #(.select(4), .width(8), .enable("false")) multiplexer_1 (
    .in0(8'h7e), .in1(8'h48), .in2(8'h3d), .in3(8'h6d), .in4(8'h4b), .in5(8'h67), .in6(8'h77), .in7(8'h4c),
    .in8(8'h7f), .in9(8'h4f), .in10(8'h5f), .in11(8'h73), .in12(8'h36), .in13(8'h79), .in14(8'h37),
    .in15(8'h17), .out({out_12, out_11, out_10, out_9, out_8, out_7, out_6, out_5}), .sel({e3, e2, e1, e0}));
  _7_Segment_Display u_7_segment_display_1 (
    .g(out_5), .f(out_6), .a(out_7), .b(out_8), .e(out_9), .d(out_10), .c(out_11), .dp(out_12));
endmodule

module Decoder_Roma (
  input  e3,
  input  e2,
  input  e1,
  input  e0,
  output a,
  output b,
  output c,
  output d,
  output e,
  output f,
  output g
);

  wire and_1_out, and_2_out, and_3_out, and_4_out, and_5_out, and_6_out, and_7_out, and_8_out, and_9_out,
       and_10_out, and_11_out, and_12_out, and_13_out, and_14_out, and_15_out, and_16_out, and_17_out,
       and_18_out, and_19_out, and_20_out, and_21_out, and_22_out, and_23_out, and_24_out, and_25_out,
       and_26_out, and_27_out, and_28_out, and_29_out, and_30_out, and_31_out, and_32_out, and_33_out,
       not_1_out, not_2_out, not_3_out, not_4_out, not_5_out, not_6_out, not_7_out, not_8_out, not_9_out,
       not_10_out, not_11_out, not_12_out, not_13_out, not_14_out, not_15_out, not_16_out, not_17_out,
       not_18_out, not_19_out, not_20_out, not_21_out, not_22_out, not_23_out, not_24_out, not_25_out,
       not_26_out, not_27_out, not_28_out, not_29_out, not_30_out, not_31_out, not_32_out, not_33_out,
       not_34_out, not_35_out, not_36_out, not_37_out, not_38_out, not_39_out, not_40_out, not_41_out,
       not_42_out, not_43_out, not_44_out;

  not not_1 (not_1_out, e2);
  and and_1 (and_1_out, not_1_out, not_2_out);
  not not_2 (not_2_out, e0);
  not not_3 (not_3_out, e3);
  and and_2 (and_2_out, not_3_out, e1);
  and and_3 (and_3_out, e2, e0);
  not not_4 (not_4_out, e2);
  and and_4 (and_4_out, e3, not_4_out, not_5_out);
  not not_5 (not_5_out, e1);
  not not_6 (not_6_out, e3);
  and and_5 (and_5_out, not_6_out, not_7_out);
  not not_7 (not_7_out, e2);
  not not_8 (not_8_out, e3);
  and and_6 (and_6_out, not_8_out, not_9_out, not_10_out);
  not not_9 (not_9_out, e1);
  not not_10 (not_10_out, e0);
  not not_11 (not_11_out, e2);
  and and_7 (and_7_out, not_11_out, not_12_out);
  not not_12 (not_12_out, e1);
  not not_13 (not_13_out, e3);
  and and_8 (and_8_out, not_13_out, e1, e0);
  and and_9 (and_9_out, e3, e1, not_14_out);
  not not_14 (not_14_out, e0);
  not not_15 (not_15_out, e3);
  and and_10 (and_10_out, not_15_out, not_16_out);
  not not_16 (not_16_out, e1);
  not not_17 (not_17_out, e3);
  and and_11 (and_11_out, not_17_out, e0);
  not not_18 (not_18_out, e3);
  and and_12 (and_12_out, not_18_out, e2);
  and and_13 (and_13_out, e3, not_19_out);
  not not_19 (not_19_out, e2);
  and and_14 (and_14_out, e3, e1, not_20_out);
  not not_20 (not_20_out, e0);
  not not_21 (not_21_out, e3);
  and and_15 (and_15_out, not_21_out, not_22_out, not_23_out);
  not not_22 (not_22_out, e2);
  not not_23 (not_23_out, e0);
  not not_24 (not_24_out, e2);
  and and_16 (and_16_out, not_24_out, e1, e0);
  not not_25 (not_25_out, e1);
  and and_17 (and_17_out, e2, not_25_out, e0);
  and and_18 (and_18_out, e2, e1, not_26_out);
  not not_26 (not_26_out, e0);
  not not_27 (not_27_out, e2);
  and and_19 (and_19_out, e3, not_27_out, not_28_out);
  not not_28 (not_28_out, e1);
  not not_29 (not_29_out, e2);
  and and_20 (and_20_out, not_29_out, not_30_out);
  not not_30 (not_30_out, e0);
  and and_21 (and_21_out, e1, not_31_out);
  not not_31 (not_31_out, e0);
  and and_22 (and_22_out, e3, e1);
  and and_23 (and_23_out, e3, e2, e0);
  not not_32 (not_32_out, e3);
  not not_33 (not_33_out, e1);
  and and_24 (and_24_out, not_32_out, not_33_out, not_34_out);
  not not_34 (not_34_out, e0);
  not not_35 (not_35_out, e3);
  and and_25 (and_25_out, not_35_out, e2, not_36_out);
  not not_36 (not_36_out, e1);
  not not_37 (not_37_out, e3);
  and and_26 (and_26_out, not_37_out, e2, not_38_out);
  not not_38 (not_38_out, e0);
  and and_27 (and_27_out, e3, not_39_out);
  not not_39 (not_39_out, e2);
  and and_28 (and_28_out, e3, e0);
  not not_40 (not_40_out, e2);
  and and_29 (and_29_out, not_40_out, e1);
  and and_30 (and_30_out, e1, not_41_out);
  not not_41 (not_41_out, e0);
  not not_42 (not_42_out, e3);
  and and_31 (and_31_out, not_42_out, e2, not_43_out);
  not not_43 (not_43_out, e1);
  and and_32 (and_32_out, e3, not_44_out);
  not not_44 (not_44_out, e2);
  and and_33 (and_33_out, e3, e0);
  or or_1 (a, and_1_out, and_2_out, and_3_out, and_4_out);
  or or_2 (b, and_5_out, and_6_out, and_7_out, and_8_out, and_9_out);
  or or_3 (c, and_10_out, and_11_out, and_12_out, and_13_out, and_14_out);
  or or_4 (d, and_15_out, and_16_out, and_17_out, and_18_out, and_19_out);
  or or_5 (e, and_20_out, and_21_out, and_22_out, and_23_out);
  or or_6 (f, and_24_out, and_25_out, and_26_out, and_27_out, and_28_out);
  or or_7 (g, and_29_out, and_30_out, and_31_out, and_32_out, and_33_out);
endmodule

module TTL (
);

  _747266 #(.ShowInternalStructure("true")) u_747266_1 ();  // open: pin1, pin2, pin3, pin4, pin5, pin6, pin13, pin12, pin11, pin10, pin9, pin8
  _7408 #(.ShowInternalStructure("true")) u_7408_1 ();  // open: pin1, pin2, pin3, pin4, pin5, pin6, pin13, pin12, pin11, pin10, pin9, pin8
  _7432 #(.ShowInternalStructure("true")) u_7432_1 ();  // open: pin1, pin2, pin3, pin4, pin5, pin6, pin13, pin12, pin11, pin10, pin9, pin8
endmodule
