// Logisim project EP02.circ as structural Verilog: 6 circuits, main circuit ULA
module SomaCompleta (
  input  a,
  input  b,
  input  CIn,
  output S,
  output COut
);

  wire and_1_out, and_2_out, xor_1_out;

  xor xor_1 (xor_1_out, a, b);
  and and_1 (and_1_out, a, b);
  xor xor_2 (S, xor_1_out, CIn);
  and and_2 (and_2_out, xor_1_out, CIn);
  or or_1 (COut, and_2_out, and_1_out);
endmodule

module ULA (
  input  bitInvert,
  input  CIn,
  input  [1:0] Opcode,
  input  a,
  input  b,
  output Result,
  output COut
);

  wire and_1_out, multiplexer_1_out, not_1_out, not_2_out, or_1_out, somacompleta_1_s;

  Multiplexer #(.enable("false")) multiplexer_1 (.in0(b), .in1(not_1_out), .out(multiplexer_1_out), .sel(bitInvert));
  not not_1 (not_1_out, b);
  SomaCompleta somacompleta_1 (.a(a), .b(multiplexer_1_out), .CIn(CIn), .S(somacompleta_1_s), .COut(COut));
  and and_1 (and_1_out, a, b);
  or or_1 (or_1_out, a, b);
  not not_2 (not_2_out, a);
  Multiplexer #(.select(2), .enable("false")) multiplexer_2 (
    .in0(and_1_out), .in1(or_1_out), .in2(not_2_out), .in3(somacompleta_1_s), .out(Result), .sel(Opcode));
endmodule

module _4Bit_ULA (
  input  [3:0] b,
  input  [3:0] a,
  input  BInvert,
  input  [1:0] OpCode,
  output [3:0] S,
  output COut
);

  wire ula_1_cout, ula_2_cout, ula_3_cout;

  ULA ula_1 (.a(a[0]), .b(b[0]), .Result(S[0]), .bitInvert(BInvert), .CIn(BInvert), .Opcode(OpCode), .COut(ula_1_cout));
  ULA ula_2 (
    .a(a[1]), .b(b[1]), .Result(S[1]), .bitInvert(BInvert), .CIn(ula_1_cout), .Opcode(OpCode),
    .COut(ula_2_cout));
  ULA ula_3 (
    .a(a[2]), .b(b[2]), .Result(S[2]), .bitInvert(BInvert), .CIn(ula_2_cout), .Opcode(OpCode),
    .COut(ula_3_cout));
  ULA ula_4 (.a(a[3]), .b(b[3]), .Result(S[3]), .bitInvert(BInvert), .CIn(ula_3_cout), .Opcode(OpCode), .COut(COut));
endmodule

module Tests (
  input  bitInvert,
  input  [1:0] OpCode,
  input  [3:0] a,
  input  [3:0] a_2,
  input  [3:0] b,
  input  [3:0] b_2,
  input  [1:0] op,
  output [3:0] s,
  output COut
);

  _4Bit_ULA u_4bit_ula_1 (.S(s), .COut(COut), .b(b_2), .a(a_2), .BInvert(bitInvert), .OpCode(OpCode));
  // Probe on {2'b00, a, b, op}
endmodule

module BigULA (
  input  [3:0] a,
  input  [3:0] b,
  input  [3:0] OpCode,
  output [3:0] s
);

  wire [3:0] and_1_out, and_2_out, and_3_out, nand_1_out, nor_1_out, not_1_out, not_2_out, not_3_out,
       not_4_out, not_5_out, not_6_out, or_1_out, or_2_out, or_3_out, xnor_1_out, xor_1_out;

  assign not_1_out = ~b;  // NOT_Gate not_1, 4 bits wide
  assign not_2_out = ~a;  // NOT_Gate not_2, 4 bits wide
  assign not_3_out = ~a;  // NOT_Gate not_3, 4 bits wide
  assign nor_1_out = ~(a | b);  // NOR_Gate nor_1, 4 bits wide
  assign not_4_out = ~a;  // NOT_Gate not_4, 4 bits wide
  assign and_1_out = not_4_out & b;  // AND_Gate and_1, 4 bits wide
  assign nand_1_out = ~(a & b);  // NAND_Gate nand_1, 4 bits wide
  assign not_5_out = ~b;  // NOT_Gate not_5, 4 bits wide
  assign xor_1_out = a ^ b;  // XOR_Gate xor_1, 4 bits wide
  assign and_2_out = a & not_1_out;  // AND_Gate and_2, 4 bits wide
  assign or_1_out = not_2_out | b;  // OR_Gate or_1, 4 bits wide
  assign xnor_1_out = ~(a ^ b);  // XNOR_Gate xnor_1, 4 bits wide
  assign and_3_out = a & b;  // AND_Gate and_3, 4 bits wide
  assign or_2_out = a | not_6_out;  // OR_Gate or_2, 4 bits wide
  assign not_6_out = ~b;  // NOT_Gate not_6, 4 bits wide
  assign or_3_out = a | b;  // OR_Gate or_3, 4 bits wide
  Multiplexer #(.select(4), .width(4), .enable("false")) multiplexer_1 (
    .in0(not_3_out), .in1(nor_1_out), .in2(and_1_out), .in3(4'b0000), .in4(nand_1_out), .in5(not_5_out),
    .in6(xor_1_out), .in7(and_2_out), .in8(or_1_out), .in9(xnor_1_out), .in10(b), .in11(and_3_out),
    .in12(4'b1111), .in13(or_2_out), .in14(or_3_out), .in15(a), .out(s), .sel(OpCode));
endmodule

module Tests_2 (
  input  [3:0] in_1,
  input  [3:0] a,
  input  [3:0] b,
  output [3:0] out_4,
  output [3:0] out_5,
  output [3:0] out_6,
  output [3:0] out_7
);

  BigULA bigula_1 (.s(out_4), .a(a), .b(b), .OpCode(in_1));
  // Probe on 4'b0010
  // Probe on 4'b0011
  // Probe on 4'b1111

  assign out_5 = 4'b0010;
  assign out_6 = 4'b0011;
  assign out_7 = 4'b1111;
endmodule
