// Logisim project Multiplicador2x2.circ as structural Verilog: 1 circuit, main circuit main
module main (
  input  a0,
  input  a1,
  input  b0,
  input  b1,
  output out_5,
  output out_6,
  output out_7,
  output out_8
);

  wire adder_2_cout, and_1_out, and_2_out, and_3_out;

  and and_1 (and_1_out, b1, a1);
  Adder #(.width(1)) adder_1 (.a(adder_2_cout), .b(and_1_out), .out(out_6), .cin(1'b0), .cout(out_5));
  and and_2 (and_2_out, a0, b1);
  and and_3 (and_3_out, a1, b0);
  Adder #(.width(1)) adder_2 (.a(and_3_out), .b(and_2_out), .out(out_7), .cin(1'b0), .cout(adder_2_cout));
  and and_4 (out_8, a0, b0);
endmodule
